# Fritzing sketch buzzereater (saved by Fritzing 0.9.3b)
circuit board: 8cm x 6cm
breadboards: 1

parts:
  Q1 = NPN-Transistor [package="TO92 [THT]"]
  D1 = Rectifier Diode [part_number=1N4001 package="300 mil [THT]"]
  R3 = Resistor [tolerance=±5% resistance=10k package=THT]
  R4 = Resistor [tolerance=±5% resistance=220 package=THT]
  S4 = Momentary Switch [package=ksa_sealed_tac_switch]
  U1 = Vibration Motor- ROB-08449 [package=vibe-motor-10mm]
  J1 = female pin header, 8 pins [form="♀ (female)"]
  Part5 = Adafruit FONA - Mini Cellular GSM Breakout
  J2 = female pin header, 12 pins [form="♀ (female)"]
  J3 = female pin header, 12 pins [form="♀ (female)"]

nets:
  N1: Q1.E, R3.Pin_0, J1.pin1, Part5.PWRKEY_5V, Part5.GND, J2.pin2
  N2: Q1.B, R4.Pin_1
  N3: Q1.C, D1.anode, U1.-
  N4: D1.cathode, S4.1, U1.+, J1.pin2, Part5.VCCIO, J2.pin4
  N5: R3.Pin_1, S4.3
  N6: R4.Pin_0, J2.pin6
  N7: S4.4, J2.pin5
  N8: J1.pin5, J3.pin1
  N9: J1.pin7, J3.pin12
  N10: J1.pin8, J3.pin11
  N11: Part5.RXD_5V, J3.pin4
  N12: Part5.TXD_5V, J2.pin9
  N13: Part5.RESET_5V, J3.pin5

notes:
  OLED
  ARDUINO
  FONA
  MOTOR
  DIODE
  NPN
  220
  BUZZER V1
  10k

custom parts:
  Adafruit FONA - Mini Cellular GSM Breakout: An all-in-one cellular phone module that lets you add voice, text, SMS and GPRS data to your project. Quad-band 850/900/1800/1900MHz - connect onto any global GSM network with any 2G SIM. Includes an onboard LiPoly battery charging circuitry so you can take your project on the go. Also works as an FM radio receiver.
